# Fritzing sketch Arduino (saved by Fritzing 0.9.1b)
breadboards: 1

parts:
  Part1 = Arduino Uno (Rev3)
  R1 = Resistor [tolerance=±5% resistance=1M package=THT]
  LED1 = RGB LED (com. cathode, rgb) [package="5 mm [THT]"]
  R2 = Resistor [tolerance=±5% resistance=220 package=THT]
  R3 = Resistor [tolerance=±5% resistance=220 package=THT]
  R4 = Resistor [tolerance=±5% resistance=220 package=THT]
  U3 = IC, DIP package, 8 pins [chip_label=ISL8487E]

nets:
  N1: Part1.D9_PWM, R2.Pin_1
  N2: Part1.D10_PWM/SS, R3.Pin_1
  N3: Part1.D11_PWM/MOSI, R4.Pin_1
  N4: Part1.D0/RX, U3.pin1
  N5: Part1.D1/TX, U3.pin4
  N6: Part1.D2, U3.pin2, U3.pin3
  N7: Part1.D3_PWM, R1.Pin_1
  N8: Part1.D4, R1.Pin_0
  N9: Part1.5V, U3.pin8
  N10: Part1.GND, LED1.common_cathode, U3.pin5
  N11: LED1.red_anode, R4.Pin_0
  N12: LED1.green_anode, R3.Pin_0
  N13: LED1.blue_anode, R2.Pin_0

notes:
  Capacitive Sensor Area
  To next node
  From previous node or +
  To RS485 Bus
