# Fritzing sketch DiscoFloor (saved by Fritzing 0.9.1b)
breadboards: 1

parts:
  IC1 = MICROCONTROLLER [part_number=Atmega168 package=dil28-3-zif_socket]
  R1 = Resistor [tolerance=±5% resistance=220 package=THT]
  R3 = Resistor [tolerance=±5% resistance=220 package=THT]
  R4 = Resistor [tolerance=±5% resistance=220 package=THT]
  R5 = Resistor [tolerance=±5% resistance=220 package=THT]
  XTAL1 = Crystal [frequency="16 Mhz" package=THT]
  C4 = Capacitor [package=cap-pth-small2]
  C3 = Capacitor [package=cap-pth-small2]
  LED1 = RGB LED (com. cathode, rgb) [package="5 mm [THT]"]
  ISL8487E_RS485 = IC, DIP package, 8 pins [chip_label=ISL8487E]

nets:
  N1: IC1.PD0(RXD), ISL8487E_RS485.pin1
  N2: IC1.PD1(TXD), ISL8487E_RS485.pin4
  N3: IC1.PD2(INT0), ISL8487E_RS485.pin2, ISL8487E_RS485.pin3
  N4: IC1.PD3(INT1), R1.Pin_0
  Cap Sensor: IC1.PD4(XCK_T0), R1.Pin_1
  5V: IC1.VCC, ISL8487E_RS485.pin8
  GND: IC1.GND, C4.2, C3.2, LED1.common_cathode, ISL8487E_RS485.pin5
  N5: IC1.PB6(XTAL1_TOSC1), XTAL1.pin_1, C3.1
  N6: IC1.PB7(XTAL2_TOSC2), XTAL1.pin_0, C4.1
  Next node: IC1.PD5(T1)
  Previous node: IC1.PD6(AIN0)
  N7: IC1.PB1(OC1A), R5.Pin_0
  N8: IC1.PB2(SS_OC1B), R3.Pin_0
  N9: IC1.PB3(MOSI_OC2), R4.Pin_0
  N10: R3.Pin_1, LED1.green_anode
  N11: R4.Pin_1, LED1.red_anode
  N12: R5.Pin_1, LED1.blue_anode
  To Bus: ISL8487E_RS485.pin6, ISL8487E_RS485.pin7

notes:
  Capacitive Sensor Area
  To next node
  To RS485 Bus
  From previous node or +
