# Fritzing sketch DiscoFloor_Arduino (saved by Fritzing 0.9.1b)
breadboards: 1

parts:
  Part1 = Arduino Uno (Rev3)
  U1 = MAX485 [package=dil08]
  R1 = Resistor [tolerance=±5% resistance=1M package=THT]
  LED1 = RGB LED (com. cathode, rgb) [package="5 mm [THT]"]
  R2 = Resistor [tolerance=±5% resistance=220 package=THT]
  R3 = Resistor [tolerance=±5% resistance=220 package=THT]
  R4 = Resistor [tolerance=±5% resistance=220 package=THT]

nets:
  N1: Part1.D9_PWM, R2.Pin_1
  N2: Part1.D10_PWM/SS, R3.Pin_1
  N3: Part1.D11_PWM/MOSI, R4.Pin_1
  N4: Part1.D0/RX, U1.RO
  N5: Part1.D1/TX, U1.DI
  N6: Part1.D2, U1.RE, U1.DE
  N7: Part1.D3_PWM, R1.Pin_1
  N8: Part1.D4, R1.Pin_0
  GND: Part1.GND, U1.GND, LED1.common_cathode
  VIN: Part1.VIN, U1.VCC
  N9: LED1.red_anode, R4.Pin_0
  N10: LED1.green_anode, R3.Pin_0
  N11: LED1.blue_anode, R2.Pin_0

notes:
  Capacitive Sensor Area
  To next node
  To previous node
  To RS485 Bus
